// Logisim project cpu.circ as structural Verilog: 1 circuit, main circuit cpu
module cpu (
);

  wire [31:0] PC_q;

  Register #(.width(32)) PC (.Q(PC_q));  // open: D, en, clk, clr
  mem InstMem (.MemAddress(PC_q));  // open: MemWriteMask, MemWriteData, clk, MemReadData
  // control_unit CU: pin names not known
  // regfile RegisterFile: pin names not known
  // ALU ArithLogicUnit: pin names not known
  // alu_control_unit ALU_Control: pin names not known
  // mem DataMem: pin names not known
endmodule
